// Logisim project BYOC-24-HI-LO.circ as structural Verilog: 4 circuits, main circuit main
module main (
  input  Run_Stop,
  input  Reset,
  input  Debug,
  input  [15:0] in_4
);

  wire byoc_i_1_ior, byoc_i_1_iow, byoc_i_1_reset_2, keyboard_1_avail, tu_1_dspclk, tu_1_kbyclk;
  wire [3:0] byoc_i_1_a_register, byoc_i_1_a_register_2, byoc_i_1_c_register, byoc_i_1_c_register_2,
       byoc_i_1_d_register, byoc_i_1_d_register_2;
  wire [6:0] keyboard_1_data, tu_1_dspout_7__0;
  wire [7:0] byoc_i_1_b_register, byoc_i_1_e_register, byoc_i_1_h_register, byoc_i_1_ioout_7__0,
       byoc_i_1_ioport_7__0, byoc_i_1_l_register, byoc_i_1_m_register, rnu_1_tuout_7__0;
  wire [15:0] byoc_i_1_adrs_15__0;
  wire [23:0] byoc_i_1_memout;

  Hex_Digit_Display hex_digit_display_1 (.value(in_4[15:12]));  // open: dp
  BYOC_I byoc_i_1 (
    .Run(Run_Stop), .Reset(Reset), .L_Register(byoc_i_1_l_register), .H_Register(byoc_i_1_h_register),
    .E_Register(byoc_i_1_e_register), .M_Register(byoc_i_1_m_register), .MemOut(byoc_i_1_memout),
    .IOR(byoc_i_1_ior), .IOW(byoc_i_1_iow), .IOInp_7__0(rnu_1_tuout_7__0),
    .IOPort_7__0(byoc_i_1_ioport_7__0), .Reset_2(byoc_i_1_reset_2), .DBA(in_4),
    .D_Register({byoc_i_1_d_register_2, byoc_i_1_d_register}),
    .C_Register({byoc_i_1_c_register_2, byoc_i_1_c_register}), .B_Register(byoc_i_1_b_register),
    .A_Register({byoc_i_1_a_register_2, byoc_i_1_a_register}), .ADRS_15__0(byoc_i_1_adrs_15__0),
    .IOOut_7__0(byoc_i_1_ioout_7__0), .DB(Debug));
  RNU rnu_1 (.IOPort_7__0(byoc_i_1_ioport_7__0), .TUOut_7__0(rnu_1_tuout_7__0));
  Hex_Digit_Display hex_digit_display_2 (.value(in_4[7:4]));  // open: dp
  Hex_Digit_Display hex_digit_display_3 (.value(in_4[11:8]));  // open: dp
  Hex_Digit_Display hex_digit_display_4 (.value(byoc_i_1_a_register));  // open: dp
  Hex_Digit_Display hex_digit_display_5 (.value(byoc_i_1_a_register_2));  // open: dp
  TU tu_1 (
    .IOR(byoc_i_1_ior), .IOW(byoc_i_1_iow), .DA(keyboard_1_avail), .KbyInp_7__0(keyboard_1_data),
    .IOPort_7__0(byoc_i_1_ioport_7__0), .TUInp_7__0(byoc_i_1_ioout_7__0), .TUOut_7__0(rnu_1_tuout_7__0),
    .DspOut_7__0(tu_1_dspout_7__0), .DspClk(tu_1_dspclk), .KbyClk(tu_1_kbyclk));
  Hex_Digit_Display hex_digit_display_6 (.value(in_4[3:0]));  // open: dp
  Hex_Digit_Display hex_digit_display_7 (.value(byoc_i_1_b_register[7:4]));  // open: dp
  Hex_Digit_Display hex_digit_display_8 (.value(byoc_i_1_b_register[3:0]));  // open: dp
  Hex_Digit_Display hex_digit_display_9 (.value(byoc_i_1_adrs_15__0[15:12]));  // open: dp
  Keyboard keyboard_1 (
    .clk(tu_1_kbyclk), .clr(byoc_i_1_reset_2), .avail(keyboard_1_avail), .data(keyboard_1_data));  // open: re
  TTY #(.rows(16), .cols(50)) tty_1 (.data(tu_1_dspout_7__0), .clk(tu_1_dspclk));  // open: we, clr
  Hex_Digit_Display hex_digit_display_10 (.value(byoc_i_1_c_register_2));  // open: dp
  Hex_Digit_Display hex_digit_display_11 (.value(byoc_i_1_c_register));  // open: dp
  Hex_Digit_Display hex_digit_display_12 (.value(byoc_i_1_adrs_15__0[7:4]));  // open: dp
  Hex_Digit_Display hex_digit_display_13 (.value(byoc_i_1_adrs_15__0[11:8]));  // open: dp
  Hex_Digit_Display hex_digit_display_14 (.value(byoc_i_1_d_register));  // open: dp
  Hex_Digit_Display hex_digit_display_15 (.value(byoc_i_1_d_register_2));  // open: dp
  Hex_Digit_Display hex_digit_display_16 (.value(byoc_i_1_adrs_15__0[3:0]));  // open: dp
  Hex_Digit_Display hex_digit_display_17 (.value(byoc_i_1_e_register[7:4]));  // open: dp
  Hex_Digit_Display hex_digit_display_18 (.value(byoc_i_1_memout[23:20]));  // open: dp
  Hex_Digit_Display hex_digit_display_19 (.value(byoc_i_1_memout[19:16]));  // open: dp
  Hex_Digit_Display hex_digit_display_20 (.value(byoc_i_1_h_register[7:4]));  // open: dp
  Hex_Digit_Display hex_digit_display_21 (.value(byoc_i_1_e_register[3:0]));  // open: dp
  Hex_Digit_Display hex_digit_display_22 (.value(byoc_i_1_memout[15:12]));  // open: dp
  Hex_Digit_Display hex_digit_display_23 (.value(byoc_i_1_memout[11:8]));  // open: dp
  Hex_Digit_Display hex_digit_display_24 (.value(byoc_i_1_l_register[7:4]));  // open: dp
  Hex_Digit_Display hex_digit_display_25 (.value(byoc_i_1_h_register[3:0]));  // open: dp
  Hex_Digit_Display hex_digit_display_26 (.value(byoc_i_1_memout[3:0]));  // open: dp
  Hex_Digit_Display hex_digit_display_27 (.value(byoc_i_1_memout[7:4]));  // open: dp
  Hex_Digit_Display hex_digit_display_28 (.value(byoc_i_1_m_register[7:4]));  // open: dp
  Hex_Digit_Display hex_digit_display_29 (.value(byoc_i_1_l_register[3:0]));  // open: dp
  Hex_Digit_Display hex_digit_display_30 (.value(byoc_i_1_m_register[3:0]));  // open: dp

  // Notes on the sheet:
  //   BYOC-FPGA
  //   RNU
  //   TU
  //   A Register
  //   B Register
  //   C Register
  //   Address
  //   Keyboard
  //   D Register
  //   E Register
  //   H Register
  //   Program Code
  //   L Register
  //   M Register
endmodule

module BYOC_I (
  input  [15:0] DBA,
  input  DB,
  input  Run,
  input  Reset,
  input  [7:0] IOInp_7__0,
  output Reset_2,
  output [15:0] ADRS_15__0,
  output [23:0] MemOut,
  output [7:0] M_Register,
  output [7:0] L_Register,
  output IOR,
  output [7:0] H_Register,
  output IOW,
  output [7:0] E_Register,
  output [7:0] D_Register,
  output [7:0] C_Register,
  output [7:0] B_Register,
  output [7:0] IOPort_7__0,
  output [7:0] A_Register,
  output [7:0] IOOut_7__0
);

  wire and_1_out, and_8_out, and_9_out, and_10_out, and_12_out, and_14_out, and_15_out, and_16_out,
       and_17_out, C0, C1, C2, C3, CALL, CIREG, CLK0, CLK1, CLK2, CLKX, clock_1_out, comparator_1_eq,
       comparator_2_eq, comparator_2_lt, comparator_3_eq, comparator_3_lt, CPII, CRT, CRTF, CS,
       decoder_1_out0, decoder_1_out1, decoder_1_out2, decoder_1_out3, decoder_1_out4, decoder_1_out5,
       decoder_1_out6, decoder_1_out7, G1_out, G2_out, G3_out, G4_2_out, G4_out, IDX, INP, JCS, JMP, JZS, LS,
       multiplexer_8_out, multiplexer_10_out, multiplexer_11_out, nor_1_out, nor_2_out, not_1_out, not_2_out,
       not_3_out, not_4_out, not_5_out, not_6_out, not_7_out, not_8_out, not_9_out, not_10_out, not_11_out,
       not_12_out, not_13_out, not_14_out, not_15_out, not_16_out, not_17_out, not_18_out, not_19_out,
       not_20_out, not_21_out, not_22_out, not_23_out, not_24_out, not_25_out, not_26_out, not_27_out,
       not_28_out, not_29_out, not_30_out, not_31_out, not_33_out, or_1_out, or_2_out, or_7_out, or_8_out,
       OUT, POP, PUSH, RClk, RET, RRO, RRSP, S1O3, STC, ZIREG, ZS;
  wire [1:0] JR_1__0;
  wire [7:0] adder_3_out, adder_5_out, adder_6_out, adder_7_out, adder_8_out, ALUR_7__0, ARAMH_7__0,
       ARAML_7__0, AROMH_7__0, AROML_7__0, DestReg_7__0, DROM_7__0, G6_out, G7_out, multiplexer_6_out,
       multiplexer_13_out, multiplexer_20_out, multiplexer_21_out, multiplexer_22_out, multiplexer_23_out,
       multiplexer_24_out, not_32_out, OP0_7__0, OP1_7__0, PV_7__0, SPReg_2_q, SPReg_q, subtractor_1_out,
       subtractor_2_out, subtractor_3_out, xor_3_out;
  wire [15:0] adder_1_out, adder_2_out, adder_4_out, IReg_15__0, multiplexer_1_out, multiplexer_2_out,
       multiplexer_3_out, multiplexer_4_out, multiplexer_5_out, multiplexer_9_out, multiplexer_14_out,
       multiplexer_15_out, multiplexer_16_out, multiplexer_17_out, RAD_15__0;

  Clock clock_1 (.out(clock_1_out));
  Multiplexer #(.select(2), .width(16), .disabled(0), .enable("false")) multiplexer_1 (
    .in0(16'h1), .in1({MemOut[15:8], IOPort_7__0}), .in2(16'h1), .in3({H_Register, L_Register}),
    .out(multiplexer_1_out), .sel({MemOut[17], JR_1__0[0]}));
  Multiplexer #(.width(16), .enable("false")) multiplexer_2 (
    .in0(DBA), .in1({16{1'b1}}), .out(multiplexer_2_out), .sel(not_1_out));
  not not_1 (not_1_out, DB);
  and G1 (G1_out, CLKX, Run);
  Multiplexer #(.select(2), .width(16), .disabled(0), .enable("false")) multiplexer_3 (
    .in0(ADRS_15__0), .in1({16{1'b0}}), .in2(RAD_15__0), .in3({16{1'b0}}), .out(multiplexer_3_out),
    .sel(JR_1__0));
  Adder #(.width(16)) adder_1 (
    .a(multiplexer_3_out), .b(multiplexer_1_out), .out(adder_1_out), .cin(1'b0));  // open: cout
  not not_2 (not_2_out, CPII);
  not not_3 (not_3_out, MemOut[23]);
  and G1_2 (CLKX, clock_1_out, ~comparator_1_eq);  // AND_Gate
  Comparator #(.width(16)) comparator_1 (.a(ADRS_15__0), .b(multiplexer_2_out), .eq(comparator_1_eq));  // open: gt, lt
  D_Flip_Flop FF0 (.clk(G1_out), .D(CLK0), .Q(CLK1), .reset(or_1_out));  // open: Qn, preset, en
  Register #(.width(16)) PReg (.D(adder_1_out), .Q(ADRS_15__0), .clk(CLK0), .clr(Reset));  // open: en
  Multiplexer #(.width(16), .enable("false")) multiplexer_4 (
    .in0(IReg_15__0), .in1({ARAMH_7__0, ARAML_7__0}), .out(multiplexer_4_out), .sel(MemOut[17]));
  Multiplexer #(.select(2), .width(16), .disabled(0), .enable("false")) multiplexer_5 (
    .in0({16{1'b0}}), .in1({ARAMH_7__0, ARAML_7__0}), .in2(16'h1), .in3({16{1'b1}}), .out(multiplexer_5_out),
    .sel(MemOut[17:16]));
  and and_1 (and_1_out, IDX, not_2_out, not_4_out);
  not not_4 (not_4_out, MemOut[18]);
  Multiplexer #(.width(8), .enable("false")) multiplexer_6 (
    .in0(ALUR_7__0), .in1(DestReg_7__0), .out(multiplexer_6_out), .sel(G2_out));
  and G2 (G2_out, RRO, MemOut[8]);
  nor nor_1 (nor_1_out, JMP, IDX, PUSH, OUT, CRTF, STC);
  Decoder #(.select(3), .disabled(0)) decoder_1 (
    .out0(decoder_1_out0), .out1(decoder_1_out1), .out2(decoder_1_out2), .out3(decoder_1_out3),
    .out4(decoder_1_out4), .out5(decoder_1_out5), .out6(decoder_1_out6), .out7(decoder_1_out7),
    .sel(MemOut[20:18]), .en(nor_1_out));
  and and_2 (CPII, MemOut[21], MemOut[22], not_3_out, MemOut[19], MemOut[16]);
  D_Flip_Flop FF2 (.clk(G1_out), .D(CLK1), .Q(CLK2), .reset(or_1_out));  // open: Qn, preset, en
  or or_1 (or_1_out, RClk, Reset);
  Adder #(.width(16)) adder_2 (.a(multiplexer_4_out), .b(multiplexer_5_out), .out(adder_2_out));  // open: cin, cout
  Register #(.width(16)) register_1 (
    .D(adder_2_out), .en(and_1_out), .Q({ARAMH_7__0, ARAML_7__0}), .clk(CLK1), .clr(Reset));
  Multiplexer #(.select(3), .width(8), .disabled(0), .enable("false")) multiplexer_7 (
    .in0(M_Register), .in1(L_Register), .in2(H_Register), .in3(E_Register), .in4(D_Register),
    .in5(C_Register), .in6(B_Register), .in7(A_Register), .out(IOOut_7__0), .sel(MemOut[17:15]));
  Multiplexer #(.select(4), .enable("false")) multiplexer_8 (
    .in0(C0), .in1(C1), .in2(C2), .in3(C3), .in4(1'b0), .in5(1'b0), .in6(1'b0), .in7(1'b0),
    .in8(OP0_7__0[7]), .in9(OP0_7__0[0]), .in10(OP0_7__0[7]), .in11(OP0_7__0[0]), .in12(CS), .in13(CS),
    .in14(1'b1), .in15(CS), .out(multiplexer_8_out), .sel(MemOut[14:11]));
  D_Flip_Flop FF2_2 (.clk(G1_out), .D(CLK2), .Q(CLK0), .preset(or_1_out));  // open: Qn, en, reset
  Register LReg (.D(multiplexer_6_out), .en(decoder_1_out1), .Q(L_Register), .clk(CLK1), .clr(Reset));
  Register HReg (.D(multiplexer_6_out), .en(decoder_1_out2), .Q(H_Register), .clk(CLK1), .clr(Reset));
  Register EReg (.D(multiplexer_6_out), .en(decoder_1_out3), .Q(E_Register), .clk(CLK1), .clr(Reset));
  Register DReg (.D(multiplexer_6_out), .en(decoder_1_out4), .Q(D_Register), .clk(CLK1), .clr(Reset));
  Register CReg (.D(multiplexer_6_out), .en(decoder_1_out5), .Q(C_Register), .clk(CLK1), .clr(Reset));
  Register BReg (.D(multiplexer_6_out), .en(decoder_1_out6), .Q(B_Register), .clk(CLK1), .clr(Reset));
  Register AReg (.D(multiplexer_6_out), .en(decoder_1_out7), .Q(A_Register), .clk(CLK1), .clr(Reset));
  nor nor_2 (nor_2_out, ALUR_7__0[0], ALUR_7__0[1], ALUR_7__0[2], ALUR_7__0[3], ALUR_7__0[4], ALUR_7__0[5], ALUR_7__0[6], ALUR_7__0[7]);
  ROM #(.addrWidth(16), .dataWidth(24)) rom_1 (.addr(ADRS_15__0), .data({MemOut[23:8], IOPort_7__0}));  // open: sel
  Multiplexer #(.select(2), .width(16), .enable("false")) multiplexer_9 (
    .in0({H_Register, L_Register}), .in1({H_Register, L_Register}), .in2({{8{1'b1}}, IOPort_7__0}),
    .in3({ARAMH_7__0, ARAML_7__0}), .out(multiplexer_9_out), .sel({LS, S1O3}));
  Multiplexer #(.enable("false")) multiplexer_10 (.in0(nor_2_out), .in1(ZIREG), .out(multiplexer_10_out), .sel(CPII));
  or or_2 (or_2_out, RRO, CPII);
  Multiplexer #(.enable("false")) multiplexer_11 (
    .in0(multiplexer_8_out), .in1(CIREG), .out(multiplexer_11_out), .sel(CPII));
  Register #(.width(1)) ZReg (.D(multiplexer_10_out), .en(or_2_out), .Q(ZS), .clk(CLK1), .clr(Reset));
  Register #(.width(1)) CReg_2 (.D(multiplexer_11_out), .en(or_2_out), .Q(CS), .clk(CLK1), .clr(Reset));
  RAM #(.addrWidth(16), .bus("separate")) ram_1 (
    .addr(multiplexer_9_out), .din(multiplexer_6_out), .data(M_Register), .str(decoder_1_out0), .clk(CLK1));  // open: sel, ld, clr
  Multiplexer #(.select(3), .width(8), .disabled(0), .enable("false")) multiplexer_12 (
    .in0(M_Register), .in1(L_Register), .in2(H_Register), .in3(E_Register), .in4(D_Register),
    .in5(C_Register), .in6(B_Register), .in7(A_Register), .out(DestReg_7__0), .sel(MemOut[20:18]));
  Multiplexer #(.select(2), .width(8), .disabled(0), .enable("false")) multiplexer_13 (
    .in0({8{1'b0}}), .in1({8{1'b1}}), .in2(8'h1), .in3({8{1'b0}}), .out(multiplexer_13_out), .sel({PUSH, POP}));
  xor xor_1 (JZS, MemOut[18], ZS);
  xor xor_2 (JCS, MemOut[18], CS);
  not not_5 (not_5_out, MemOut[20]);
  not not_6 (not_6_out, MemOut[19]);
  not not_7 (not_7_out, MemOut[20]);
  not not_8 (not_8_out, MemOut[17]);
  Adder adder_3 (.a(SPReg_q), .b(multiplexer_13_out), .out(adder_3_out));  // open: cin, cout
  not not_9 (not_9_out, MemOut[21]);
  not not_10 (not_10_out, MemOut[22]);
  not not_11 (not_11_out, MemOut[8]);
  not not_12 (not_12_out, MemOut[9]);
  not not_13 (not_13_out, MemOut[22]);
  not not_14 (not_14_out, MemOut[9]);
  not not_15 (not_15_out, MemOut[22]);
  not not_16 (not_16_out, MemOut[8]);
  not not_17 (not_17_out, MemOut[22]);
  not not_18 (not_18_out, MemOut[21]);
  not not_19 (not_19_out, MemOut[20]);
  not not_20 (not_20_out, MemOut[23]);
  not not_21 (not_21_out, MemOut[21]);
  not not_22 (not_22_out, MemOut[22]);
  not not_23 (not_23_out, MemOut[21]);
  not not_24 (not_24_out, MemOut[23]);
  not not_25 (not_25_out, MemOut[21]);
  not not_26 (not_26_out, MemOut[19]);
  not not_27 (not_27_out, MemOut[21]);
  not not_28 (not_28_out, MemOut[21]);
  not not_29 (not_29_out, MemOut[11]);
  Register SPReg (.D(adder_3_out), .Q(SPReg_q), .clk(CLK1), .clr(or_7_out));  // open: en
  and and_3 (RET, MemOut[23], MemOut[22], not_9_out, MemOut[20]);
  and and_4 (INP, MemOut[23], not_10_out, MemOut[21], not_11_out, not_12_out);
  and and_5 (OUT, MemOut[23], not_13_out, MemOut[21], MemOut[8], not_14_out);
  and and_6 (POP, MemOut[23], not_15_out, MemOut[21], not_16_out, MemOut[9]);
  and and_7 (PUSH, MemOut[23], not_17_out, MemOut[21], MemOut[8], MemOut[9]);
  and G2_2 (CALL, MemOut[23], MemOut[22], not_18_out, not_19_out);
  and G2_3 (LS, not_20_out, MemOut[22], not_21_out);
  and G2_4 (RRO, MemOut[23], not_22_out, not_23_out);
  and G3 (G3_out, MemOut[23], MemOut[22], MemOut[21], MemOut[20]);
  and G4 (G4_out, MemOut[23], MemOut[22], MemOut[21], JZS, not_5_out, not_6_out);
  and G4_2 (G4_2_out, MemOut[23], MemOut[22], MemOut[21], JCS, not_7_out, MemOut[19]);
  and G5 (JMP, MemOut[23], MemOut[22], MemOut[21]);
  and G5_2 (IDX, not_24_out, MemOut[22], MemOut[21]);
  and and_8 (and_8_out, MemOut[23], MemOut[22], not_25_out, MemOut[20], not_26_out);
  and and_9 (and_9_out, MemOut[23], MemOut[22], not_27_out, MemOut[20], MemOut[19], not_8_out, JZS);
  and and_10 (and_10_out, MemOut[23], MemOut[22], not_28_out, MemOut[20], MemOut[19], MemOut[17], JCS);
  and and_11 (STC, RRO, MemOut[14], MemOut[13], MemOut[12], not_29_out);
  or or_3 (S1O3, MemOut[8], MemOut[10]);
  not not_30 (not_30_out, POP);
  or G4_3 (JR_1__0[0], G3_out, G4_out, G4_2_out, CALL);
  or or_4 (JR_1__0[1], and_8_out, and_9_out, and_10_out);
  RAM #(.bus("separate")) ram_2 (
    .addr(SPReg_q), .din(IOOut_7__0), .data(PV_7__0), .str(PUSH), .clk(CLK2), .clr(Reset));  // open: sel, ld
  and and_12 (and_12_out, IOPort_7__0[0], IOPort_7__0[1], IOPort_7__0[2], IOPort_7__0[3], IOPort_7__0[4], IOPort_7__0[5], IOPort_7__0[6], IOPort_7__0[7], IOW);
  and and_13 (RClk, CLK2, not_30_out);
  or or_5 (CRTF, CALL, RET);
  or or_6 (CRT, CALL, JR_1__0[1]);
  Multiplexer #(.width(16), .enable("false")) multiplexer_14 (
    .in0({MemOut[15:8], IOPort_7__0}), .in1({H_Register, L_Register}), .out(multiplexer_14_out),
    .sel(MemOut[20]));
  Multiplexer #(.width(16), .enable("false")) multiplexer_15 (
    .in0({AROMH_7__0, AROML_7__0}), .in1({H_Register, L_Register}), .out(multiplexer_15_out), .sel(MemOut[20]));
  and G11 (IOR, INP, CLK1);
  and G12 (IOW, CLK1, OUT);
  Comparator #(.width(16)) comparator_2 (
    .a({ARAMH_7__0, ARAML_7__0}), .b(multiplexer_14_out), .eq(comparator_2_eq), .lt(comparator_2_lt));  // open: gt
  Comparator #(.width(16)) comparator_3 (
    .a(multiplexer_15_out), .b({MemOut[15:8], IOPort_7__0}), .eq(comparator_3_eq), .lt(comparator_3_lt));  // open: gt
  Multiplexer #(.width(16), .enable("false")) multiplexer_16 (
    .in0(IReg_15__0), .in1({AROMH_7__0, AROML_7__0}), .out(multiplexer_16_out), .sel(MemOut[17]));
  Multiplexer #(.select(2), .width(16), .disabled(0), .enable("false")) multiplexer_17 (
    .in0({16{1'b0}}), .in1({AROMH_7__0, AROML_7__0}), .in2(16'h1), .in3({16{1'b1}}),
    .out(multiplexer_17_out), .sel(MemOut[17:16]));
  and and_14 (and_14_out, IOOut_7__0[1], and_12_out);
  and and_15 (and_15_out, and_12_out, IOOut_7__0[0]);
  Multiplexer #(.enable("false")) multiplexer_18 (
    .in0(comparator_2_eq), .in1(comparator_3_eq), .out(ZIREG), .sel(MemOut[18]));
  Multiplexer #(.enable("false")) multiplexer_19 (
    .in0(comparator_2_lt), .in1(comparator_3_lt), .out(CIREG), .sel(MemOut[18]));
  Adder #(.width(16)) adder_4 (.a(multiplexer_16_out), .b(multiplexer_17_out), .out(adder_4_out));  // open: cin, cout
  and and_16 (and_16_out, IDX, MemOut[18], not_31_out);
  not not_31 (not_31_out, CPII);
  Adder adder_5 (.a(SPReg_2_q), .b(multiplexer_20_out), .out(adder_5_out));  // open: cin, cout
  Multiplexer #(.select(2), .width(8), .disabled(0), .enable("false")) multiplexer_20 (
    .in0({8{1'b0}}), .in1({8{1'b1}}), .in2(8'h1), .in3({8{1'b0}}), .out(multiplexer_20_out),
    .sel({CALL, JR_1__0[1]}));
  or or_7 (or_7_out, and_14_out, Reset);
  or or_8 (or_8_out, and_15_out, Reset);
  Adder adder_6 (.a(OP0_7__0), .b(OP1_7__0), .out(adder_6_out), .cin(1'b0), .cout(C0));
  Subtractor subtractor_1 (.a(OP0_7__0), .b(OP1_7__0), .out(subtractor_1_out), .bin(1'b0), .bout(C1));
  Adder adder_7 (.a(OP0_7__0), .b(OP1_7__0), .out(adder_7_out), .cin(CS), .cout(C2));
  Subtractor subtractor_2 (.a(OP0_7__0), .b(OP1_7__0), .out(subtractor_2_out), .bin(CS), .bout(C3));
  Multiplexer #(.width(8), .enable("false")) multiplexer_21 (
    .in0(IOOut_7__0), .in1(IOPort_7__0), .out(multiplexer_21_out), .sel(RRSP));
  and G2_5 (RRSP, RRO, MemOut[9]);
  Register #(.width(16)) register_2 (
    .D(adder_4_out), .en(and_16_out), .Q({AROMH_7__0, AROML_7__0}), .clk(CLK1), .clr(Reset));
  Register #(.trigger("falling")) SPReg_2 (.D(adder_5_out), .en(CRT), .Q(SPReg_2_q), .clk(CLK0), .clr(or_8_out));
  assign G6_out = OP0_7__0 & OP1_7__0;  // AND_Gate G6, 8 bits wide
  assign G7_out = OP0_7__0 | OP1_7__0;  // OR_Gate G7, 8 bits wide
  assign xor_3_out = OP0_7__0 ^ OP1_7__0;  // XOR_Gate xor_3, 8 bits wide
  assign not_32_out = ~OP1_7__0;  // NOT_Gate not_32, 8 bits wide
  Multiplexer #(.select(2), .width(8), .enable("false")) multiplexer_22 (
    .in0(M_Register), .in1(M_Register), .in2(IOOut_7__0), .in3(DROM_7__0), .out(multiplexer_22_out),
    .sel(MemOut[9:8]));
  Multiplexer #(.select(3), .width(8), .enable("false")) multiplexer_23 (
    .in0(IOOut_7__0), .in1(IOOut_7__0), .in2(IOOut_7__0), .in3(IOOut_7__0), .in4(ARAML_7__0),
    .in5(ARAMH_7__0), .in6(AROML_7__0), .in7(AROMH_7__0), .out(multiplexer_23_out),
    .sel({MemOut[9:8], IOPort_7__0[7]}));
  Multiplexer #(.width(8), .enable("false")) multiplexer_24 (
    .in0(IOInp_7__0), .in1(PV_7__0), .out(multiplexer_24_out), .sel(MemOut[9]));
  Multiplexer #(.select(3), .width(8), .disabled(0), .enable("false")) multiplexer_25 (
    .in0(IOPort_7__0), .in1(multiplexer_23_out), .in2(multiplexer_22_out), .in3({8{1'b0}}),
    .in4(multiplexer_21_out), .in5(multiplexer_24_out), .in6({8{1'b0}}), .in7({8{1'b0}}), .out(OP1_7__0),
    .sel(MemOut[23:21]));
  ROM #(.addrWidth(16)) rom_2 (.addr({AROMH_7__0, AROML_7__0}), .data(DROM_7__0));  // open: sel
  Multiplexer #(.width(16), .enable("false")) multiplexer_26 (
    .in0({H_Register, L_Register}), .in1({MemOut[15:8], IOPort_7__0}), .out(IReg_15__0), .sel(and_17_out));
  not not_33 (not_33_out, MemOut[16]);
  Multiplexer #(.select(3), .width(8), .disabled(0), .enable("false")) multiplexer_27 (
    .in0({8{1'b0}}), .in1({8{1'b0}}), .in2({8{1'b0}}), .in3({8{1'b0}}), .in4(DestReg_7__0), .in5({8{1'b0}}),
    .in6({8{1'b0}}), .in7({8{1'b0}}), .out(OP0_7__0), .sel(MemOut[23:21]));
  and and_17 (and_17_out, MemOut[19], not_33_out);
  RAM #(.dataWidth(16), .bus("separate")) ram_3 (
    .addr(SPReg_2_q), .din(ADRS_15__0), .data(RAD_15__0), .str(CALL), .clk(CLK1), .clr(Reset));  // open: sel, ld
  Multiplexer #(.select(4), .width(8), .disabled(0), .enable("false")) multiplexer_28 (
    .in0(adder_6_out), .in1(subtractor_1_out), .in2(adder_7_out), .in3(subtractor_2_out), .in4(G6_out),
    .in5(G7_out), .in6(xor_3_out), .in7(not_32_out), .in8({OP0_7__0[6:0], 1'b0}),
    .in9({1'b0, OP0_7__0[7:1]}), .in10({OP0_7__0[6:0], CS}), .in11({CS, OP0_7__0[7:1]}), .in12(adder_8_out),
    .in13(subtractor_3_out), .in14({8{1'b0}}), .in15({8{1'b0}}), .out(ALUR_7__0), .sel(MemOut[14:11]));
  Adder adder_8 (.a(8'h1), .b(OP0_7__0), .out(adder_8_out), .cin(1'b0));  // open: cout
  Subtractor subtractor_3 (.a(OP0_7__0), .b(8'h1), .out(subtractor_3_out), .bin(1'b0));  // open: bout

  assign MemOut[7:0] = IOPort_7__0;
  assign Reset_2 = Reset;

  // Other names for the same wires on the sheet: LDI0 = MemOut[16]; PROM_23__0[23:0] = {MemOut[23:8], IOPort_7__0};
  //   Srce_2__0[2:0] = MemOut[17:15]; LDI1 = MemOut[17]; RETURN = JR_1__0[1]; AReg_7__0[7:0] = A_Register;
  //   BReg_7__0[7:0] = B_Register; CReg_7__0[7:0] = C_Register; Dest_2__0[2:0] = MemOut[20:18]; LDI2 = MemOut[18];
  //   LDI3 = MemOut[19]; LDI4 = MemOut[20]; DReg_7__0[7:0] = D_Register; EReg_7__0[7:0] = E_Register;
  //   HLReg_15__0[15:0] = {H_Register, L_Register}; LReg_7__0[7:0] = L_Register; HReg_7__0[7:0] = H_Register;
  //   IRAM_15__0[15:0] = {ARAMH_7__0, ARAML_7__0}; IROM_15__0[15:0] = {AROMH_7__0, AROML_7__0}; JUMP = JR_1__0[0];
  //   MReg_7__0[7:0] = M_Register; SrceReg_7__0[7:0] = IOOut_7__0; Type_2__0[2:0] = MemOut[23:21];
  //   UV_15__0[15:0] = {MemOut[15:8], IOPort_7__0}; V_7__0[7:0] = IOPort_7__0;
  //   S02[2:0] = {MemOut[9:8], IOPort_7__0[7]}; SPC0 = IOPort_7__0[7]; S12[1:0] = MemOut[9:8]; SPC1 = MemOut[8];
  //   U_7__0[7:0] = MemOut[15:8]; SPC2 = MemOut[9]; SPC3 = MemOut[10]; OPC_3__0[3:0] = MemOut[14:11]

  // Notes on the sheet:
  //   IOInp_7__0: pull=up
  //   M1
  //   Program ROM
  //   M5
  //   contents of rom_1 (hex, n*v repeats v):
  //   c00045 6c0000 c00022 c00048 c00048 6c0015 c00022 c00048 6c0030 c00022 c00048 c00028 100000 906000
  //   c00048 6c0044 c00022 c00033 9d8900 e0001b ec0018 6c007e c00022 f0000d 6c0068 c00022 f0000d 6c0051
  //   c00022 40000 c00038 6c0060 c00022 f00004 5c0300 9fa800 d80000 c00084 660000 f00022 6c0093 c00022
  //   bc0000 9c2240 e0002a bc0001 ac0002 8c0a65 ec002f 8c0265 d00000 c0004b 80000 40000 c00067 d00000
  //   a20300 a18300 40000 140064 c00078 14000a c00078 3e0000 9c0230 c00084 ac0200 b00200 d00000 1c000c
  //   c00084 d00000 1c000a c00084 d00000 a20300 a18300 80000 40000 140000 c00062 9c0b08 e40059 96a800
  //   e00050 946800 840a01 881a00 f00050 238000 946000 840201 881200 9c0b0a e40050 ac0200 b00200 d00000
  //   bc0000 9c2240 e00062 bc0001 f00084 1c0000 340000 940b0a d80000 940a30 9e8000 840201 881200 800b0a
  //   d80000 378000 9f8000 9f8000 9e8000 9f8000 340000 f0006b 800ff 886000 928800 ec0079 928000 888900
  //   e40080 d00000 846800 3d0000 9c0230 f00084 a38300 bc0000 9c2280 e40085 bc0200 a38101 d00000 620000
  //   620000 5c0100 c0046e 620000 9c0b0d e4008d bc0000 9c2240 e00082 bc0001 9c0b5c e00005 f00082 440002
  //   480003 600000 440004 480005 790000 e40016 f00005 c00478 6c008e c0047e 440000 480001 140000 c00150
  //   f00005 c00172 c001a8 ac0200 b00200 c00136 ec0491 600000 f00016 c00172 c001a8 140080 c00172 9c0b3c
  //   e400b9 942a01 f000c4 9c0b3e e400bd 942a02 f000c4 9c0b3d e400c1 942a04 f000c4 940b80 ec0491 f000c9
  //   620000 940b80 e800c9 942207 f000b4 c00172 428218 c001a8 c00293 a40200 a80200 540018 3d0000 9ca800
  //   e400d7 3e8000 9c2204 e4001d f000e1 880b80 e800dd 3e8000 9c2201 e4001d f000e1 3e8000 9c2202 e4001d
  //   f000e1 5c0100 9c0b0d e00026 620000 f000e1 280280 240200 a10300 a08300 f000a9 a40200 a80200 600000
  //   f000e1 c00172 c0024c ec0493 a10300 a08300 3c0200 438219 3c0280 43821a 1c003f c0046e c00346 680000
  //   c00172 c00263 c0027f 440019 48001a 600000 f00026 c00333 f00005 240200 280280 c00333 600000 c00172
  //   c00263 a40200 a80200 6c00ae 84a800 e0011a 660000 5c0300 9c0bfe e4010e 660000 5c0300 9c0bff e0049b
  //   846800 f0010e 40000 80000 5c0300 9fa800 e00124 238000 840201 881200 660000 f0011c d c0035e ec000f
  //   c003a0 660000 5c0300 9c0bfe e00005 f0011a 440006 480007 600000 630000 440100 80000 610000 630000
  //   f00026 440002 480003 540004 580005 8b0900 e4013e 868900 d80000 820900 e40148 840201 881200 818900
  //   e4014a 840a01 881a00 807000 d00000 840201 881200 840201 881200 3c0000 878000 881200 f0013a a38300
  //   a20300 a18300 c0010 100027 c00166 c00e8 100003 c00166 c0064 100000 c00166 c000a 100000 c00166 840230
  //   3c8000 c0046e ac0200 b00200 bc0200 d00000 1c00ff 9c0201 858800 8a1800 ec0167 858000 8a1000 9e8900
  //   d80000 946800 9c0230 f0046e 5c0100 9c0b20 dc0000 620000 f00172 300280 2c0200 6c0018 140000 2a0000
  //   258000 600000 580100 9822df 5c0300 9c227f 9f0900 e40191 5c0300 9c0b80 ec019b 660000 620000 5c0100
  //   9c0b41 ec017e 2a0000 258000 600000 9fa000 d00000 5c0300 9c0b80 660000 e80191 5c0300 9fa800 620000
  //   e0018c 946000 f0017b 620000 807000 d00000 40053 80000 96c000 868000 881200 640000 440300 660000
  //   480300 d00000 5c0100 9c0b2b e401ad 620000 f001b4 5c0100 9c0b2d e401b4 620000 c001c5 c00320 f001b5
  //   c001c5 5c0100 9c0b2b e401bc 620000 c001c5 c00289 f001b5 5c0100 9c0b2d e401c4 620000 c001c5 c00320
  //   c00289 f001b5 d00000 c001dc 5c0100 9c0b2a e401cd 620000 c001dc c002a0 f001c6 5c0100 9c0b2f e401d4
  //   620000 c001dc c002cd f001c6 5c0100 9c0b25 e401db 620000 c001dc c00311 f001c6 d00000 c001f0 da0000
  //   c00259 da0000 c00263 da0000 5c0100 9c0b28 e40497 620000 c001a8 9c0b29 e40497 620000 d00000 5c0100
  //   9c0b20 dc0000 620000 f001eb c00177 de0000 940b0e e40233 c00172 9c0b28 e40485 620000 c001a8 c00172
  //   9c0b29 e40485 620000 a40200 a80200 840b00 e00206 840b01 e00235 840b02 e0023f f0049d 800ff 40015
  //   180008 3c0000 9fc000 9c1200 9fc000 9c1200 9fc000 9c1200 9c3000 9fd000 9fd000 846800 846800 846800
  //   3c0000 9fd000 238000 846000 3c0000 9fd000 238000 846000 3c0000 9fd000 238000 846000 3c0000 9fd000
  //   238000 986800 e40209 480014 440015 882203 880b03 e00231 ec0206 a10300 a08300 807000 d00000 840be8
  //   f0022c 807000 d00000 bc0002 438212 9c2207 9c6800 e40238 bc0002 9fd000 9c32aa 438213 f0020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
  //   Data RAM
  //   M2
  //   A0
  //   Push/Pop Stack PPRAM
  //   M4
  //   S12
  //   A1
  //   S10
  //   S7
  //   S7
  //   S8
  //   S9
  //   S11
  //   S12
  //   Data ROM
  //   contents of rom_2 (hex, n*v repeats v):
  //   4e 75 6d 62 65 72 20 47 75 65 73 73 69 6e 67 20 47 61 6d 65 0 49 20 61 6d 20 74 68 69 6e 6b 69 6e 67
  //   20 6f 66 20 61 20 6e 75 6d 62 65 72 20 0 62 65 74 77 65 65 6e 20 31 20 61 6e 64 20 31 30 30 2e 20 0
  //   59 6f 75 72 20 67 75 65 73 73 3f 20 0 59 6f 75 20 67 6f 74 20 69 74 20 69 6e 20 0 20 74 72 69 65 73
  //   2e 0 54 6f 6f 20 68 69 67 68 2e 20 20 54 72 79 20 61 67 61 69 6e 2e 0 54 6f 6f 20 6c 6f 77 2e 20 20
  //   54 72 79 20 61 67 61 69 6e 2e 0 50 72 65 73 73 20 61 6e 79 20 6b 65 79 20 74 6f 20 63 6f 6e 74 69 6e
  //   75 65 2e 20 2e 20 2e 0 65 74 20 61 3d 31 0 32 30 20 70 72 69 6e 74 20 61 0 33 30 20 6c 65 74 20 61
  //   3d 61 2b 31 0 34 30 20 69 66 20 61 3e 31 30 20 74 68 65 6e 20 36 30 0 35 30 20 67 6f 74 6f 20 32 30
  //   0 36 30 20 73 74 6f 70 0 fe 31 30 20 69 3d 30 0 31 31 20 6c 3d 30 0 31 32 20 68 3d 30 0 32 30 20 72
  //   3d 72 6e 64 28 30 29 0 32 32 20 69 66 20 72 3e 39 39 39 20 74 68 65 6e 20 32 30 0 33 30 20 69 66 20
  //   72 3e 35 30 30 20 74 68 65 6e 20 36 30 0 34 30 20 6c 3d 6c 2b 31 0 34 35 20 67 6f 74 6f 20 31 30 30
  //   0 36 30 20 68 3d 68 2b 31 0 31 30 30 20 69 3d 69 2b 31 0 31 31 30 20 69 66 20 69 3c 31 4*30 20 74 68
  //   65 6e 20 32 30 0 31 32 30 20 70 72 69 6e 74 20 69 2c 6c 2c 68 0 31 33 30 20 73 74 6f 70 0 fe 31 30
  //   20 70 72 69 6e 74 0 31 35 20 70 72 69 6e 74 20 22 48 69 67 68 2f 4c 6f 77 20 47 75 65 73 73 69 6e 67
  //   20 47 61 6d 65 22 0 32 30 20 70 72 69 6e 74 0 32 35 20 70 72 69 6e 74 20 22 49 20 61 6d 20 74 68 69
  //   6e 6b 69 6e 67 20 6f 66 20 61 20 6e 75 6d 62 65 72 20 62 65 74 77 65 65 6e 20 31 20 61 6e 64 20 31
  //   30 30 2e 22 0 33 30 20 67 6f 73 75 62 20 31 30 30 0 33 35 20 74 3d 30 0 34 30 20 6c 65 74 20 74 3d
  //   74 2b 31 0 34 35 20 70 72 69 6e 74 20 22 59 6f 75 72 20 67 75 65 73 73 22 3b 0 35 30 20 69 6e 70 75
  //   74 20 67 0 35 35 20 69 66 20 67 3c 3e 72 20 74 68 65 6e 20 37 30 0 36 30 20 70 72 69 6e 74 20 22 59
  //   6f 75 20 67 6f 74 20 69 74 20 69 6e 20 22 3b 74 3b 22 74 72 69 65 73 22 0 36 35 20 67 6f 74 6f 20 31
  //   30 0 37 30 20 74 3d 74 2b 31 0 37 35 20 69 66 20 67 3e 72 20 74 68 65 6e 20 39 30 0 38 30 20 70 72
  //   69 6e 74 20 22 54 6f 6f 20 6c 6f 77 2e 20 54 72 79 20 61 67 61 69 6e 22 0 38 35 20 67 6f 74 6f 20 34
  //   30 0 39 30 20 70 72 69 6e 74 20 22 54 6f 6f 20 68 69 67 68 2e 20 20 54 72 79 20 61 67 61 69 6e 2e 22
  //   0 39 35 20 67 6f 74 6f 20 34 30 0 31 30 30 20 72 3d 72 6e 64 28 30 29 0 31 30 35 20 72 3d 72 25 31
  //   30 30 2b 31 0 31 31 30 20 72 65 74 75 72 6e 0 fe 31 30 20 61 3d 31 30 0 32 30 20 62 3d 32 0 33 30 20
  //   63 3d 33 0 34 30 20 64 3d 2d 32 2a 28 31 36 2f 62 2b 33 2a 61 2a 28 63 2b 34 2a 62 2f 28 63 2d 62 29
  //   29 2b 31 36 29 0 35 30 20 70 72 69 6e 74 20 64 0 fe 31 30 20 70 72 69 6e 74 20 22 50 72 69 6e 74 20
  //   53 71 75 61 72 65 73 20 44 65 6d 6f 22 0 32 30 20 70 72 69 6e 74 0 33 30 20 70 72 69 6e 74 20 22 45
  //   6e 74 65 72 20 73 74 61 72 74 69 6e 67 20 6e 75 6d 62 65 72 22 3b 0 34 30 20 69 6e 70 75 74 20 73 0
  //   35 30 20 70 72 69 6e 74 20 22 45 6e 74 65 72 20 65 6e 64 69 6e 67 20 6e 75 6d 62 65 72 22 3b 0 36 30
  //   20 69 6e 70 75 74 20 65 0 37 30 20 70 72 69 6e 74 0 38 30 20 70 72 69 6e 74 20 22 4e 75 6d 62 65 72
  //   22 2c 22 53 71 75 61 72 65 22 0 39 30 20 70 72 69 6e 74 20 73 2c 73 2a 73 0 31 30 30 20 73 3d 73 2b
  //   31 0 31 31 30 20 69 66 20 73 3c 3d 65 20 74 68 65 6e 20 39 30 0 31 32 30 20 73 74 6f 70 0 fe ff
  //   Call/Return Stack CRRAM
endmodule

module TU (
  input  IOR,
  input  IOW,
  input  DA,
  input  [6:0] KbyInp_7__0,
  input  [7:0] IOPort_7__0,
  input  [7:0] TUInp_7__0,
  output [7:0] TUOut_7__0,
  output [6:0] DspOut_7__0,
  output DspClk,
  output KbyClk
);

  wire UnitSel;

  and G2 (UnitSel, ~IOPort_7__0[1], ~IOPort_7__0[2], ~IOPort_7__0[3], ~IOPort_7__0[4], ~IOPort_7__0[5], ~IOPort_7__0[6], ~IOPort_7__0[7]);  // AND_Gate
  and G0 (KbyClk, IOR, IOPort_7__0[0], UnitSel);
  and G1 (DspClk, IOW, IOPort_7__0[0], UnitSel);
  Multiplexer #(.width(8)) multiplexer_1 (
    .in0({1'b0, DA, {6{1'b0}}}), .in1({1'b0, KbyInp_7__0}), .out(TUOut_7__0), .sel(IOPort_7__0[0]),
    .en(UnitSel));

  assign DspOut_7__0 = TUInp_7__0[6:0];

  // Other names for the same wires on the sheet: PortSel = IOPort_7__0[0]

  // Notes on the sheet:
  //   TUOut_7__0: pull=up
  //   S0
  //   S1
  //   S2
  //   S4
  //   S3
  //   S5
  //   M0
endmodule

module RNU (
  input  [7:0] IOPort_7__0,
  output [7:0] TUOut_7__0
);

  wire CLKX, clock_1_out, G2_out;
  wire [7:0] counter_1_q, counter_2_q;

  Clock clock_1 (.out(clock_1_out));
  Counter #(.max('h64)) counter_1 (.Q(counter_1_q), .clk(clock_1_out));  // open: load, D, count, carry, clr
  and G2 (G2_out, ~IOPort_7__0[0], IOPort_7__0[1], ~IOPort_7__0[2], ~IOPort_7__0[3], ~IOPort_7__0[4], ~IOPort_7__0[5], ~IOPort_7__0[6], ~IOPort_7__0[7]);  // AND_Gate
  assign TUOut_7__0 = G2_out ? counter_1_q : 8'bz;  // Controlled_Buffer controlled_buffer_1
  Counter #(.max('h64)) counter_2 (.Q(counter_2_q), .clk(CLKX));  // open: load, D, count, carry, clr

  // Notes on the sheet:
  //   TUOut_7__0: pull=up
  //   S0
endmodule
